# Fritzing sketch arduino_schematic (saved by Fritzing 0.9.3b)
breadboards: 1

parts:
  bread = Arduino Nano (Rev3.0)
  R1 = Rotary Potentiometer (Large) [maximum_resistance=10kΩ package=THT]
  R2 = Rotary Potentiometer (Large) [maximum_resistance=10kΩ package=THT]
  R3 = Rotary Potentiometer (Large) [maximum_resistance=10kΩ package=THT]
  R4 = Rotary Potentiometer (Large) [maximum_resistance=10kΩ package=THT]
  R5 = Rotary Potentiometer (Large) [maximum_resistance=10kΩ package=THT]
  S1 = Momentary Switch [package=ksa_sealed_tac_switch]
  R6 = Resistor [tolerance=±5% resistance=100k package=THT]

nets:
  N1: bread.D2, S1.1, R6.Pin_1
  N2: bread.GND, R1.leg2, R2.leg2, R3.leg2, R4.leg2, R5.leg2
  N3: bread.5V, R1.leg1, R2.leg1, R3.leg1, R4.leg1
  N4: bread.A4, R5.wiper
  N5: bread.A3, R4.wiper
  N6: bread.A2, R3.wiper
  N7: bread.A1, R2.wiper
  N8: bread.A0, R1.wiper
  N9: R5.leg1, S1.3
